// Logisim project MUX_1_BIT.circ as structural Verilog: 1 circuit, main circuit MUX_1BIT
module MUX_1BIT (
  input  E0,
  input  E1,
  input  E2,
  input  E3,
  input  S1,
  input  S0,
  output Y
);

  wire and_1_out, and_2_out, and_3_out, and_4_out, not_1_out, not_2_out, not_3_out, not_4_out;

  not not_1 (not_1_out, S1);
  not not_2 (not_2_out, S0);
  not not_3 (not_3_out, S1);
  not not_4 (not_4_out, S0);
  and and_1 (and_1_out, E0, not_1_out, not_2_out);
  and and_2 (and_2_out, E1, not_3_out, S0);
  and and_3 (and_3_out, E2, S1, not_4_out);
  and and_4 (and_4_out, E3, S1, S0);
  or or_1 (Y, and_1_out, and_2_out, and_3_out, and_4_out);
endmodule
