// Logisim project 1-Registrador FLIP FLOP D.circ as structural Verilog: 1 circuit, main circuit Registrador FLIP FLOP D
module Registrador_FLIP_FLOP_D (
  input  EN,
  input  D,
  output Q,
  output Q_minus
);

  wire and_1_out, and_2_out, not_1_out;

  not not_1 (not_1_out, D);
  and and_1 (and_1_out, not_1_out, EN);
  and and_2 (and_2_out, EN, D);
  nor nor_1 (Q, and_1_out, Q_minus);
  nor nor_2 (Q_minus, Q, and_2_out);
endmodule
