// Logisim project 1-Registrador FLIP FLOP JK.circ as structural Verilog: 1 circuit, main circuit Registradores FLIP FLOP
module Registradores_FLIP_FLOP (
  input  SET,
  input  J,
  input  K,
  input  CLEAR,
  output Q,
  output Q_NEGADO
);

  wire CLOCK_out, nand_1_out, nand_2_out, nand_3_out, nand_4_out, nand_5_out, nand_6_out, not_1_out,
       not_2_out, not_3_out, not_4_out;

  Button CLOCK (.out(CLOCK_out));
  not not_1 (not_1_out, CLOCK_out);
  nand nand_1 (nand_1_out, Q_NEGADO, J, not_1_out);
  nand nand_2 (nand_2_out, not_1_out, K, Q);
  not not_2 (not_2_out, SET);
  not not_3 (not_3_out, CLEAR);
  nand nand_3 (nand_3_out, not_2_out, nand_1_out, nand_4_out);
  nand nand_4 (nand_4_out, nand_3_out, nand_2_out, not_3_out);
  not not_4 (not_4_out, not_1_out);
  nand nand_5 (nand_5_out, nand_3_out, not_4_out, not_3_out);
  nand nand_6 (nand_6_out, not_2_out, not_4_out, nand_4_out);
  nand nand_7 (Q, not_2_out, nand_5_out, Q_NEGADO);
  nand nand_8 (Q_NEGADO, Q, nand_6_out, not_3_out);
endmodule
