// Logisim project 10-ULA de 8 bits com as seguintes operaçΣes AND OR NOT NOR NAND XOR.circ as structural Verilog: 10 circuits, main circuit main
module main (
  input  [7:0] in_1,
  input  [7:0] in_2,
  input  [3:0] in_3,
  input  in_4,
  input  in_5,
  output [7:0] out_6,
  output out_7,
  output out_8
);

  wire [7:0] and_1_out, deslocamento_1_out_2, deslocamento_para_direita_1_out_2, nand_1_out, nor_1_out,
       not_1_out, or_1_out, somador_1_q, \subtração_de_8bits_1_s , xor_1_out;

  assign and_1_out = in_1 & in_2;  // AND_Gate and_1, 8 bits wide
  assign or_1_out = in_1 | in_2;  // OR_Gate or_1, 8 bits wide
  assign not_1_out = ~in_1;  // NOT_Gate not_1, 8 bits wide
  assign nor_1_out = ~(in_1 | in_2);  // NOR_Gate nor_1, 8 bits wide
  assign nand_1_out = ~(in_1 & in_2);  // NAND_Gate nand_1, 8 bits wide
  assign xor_1_out = in_1 ^ in_2;  // XOR_Gate xor_1, 8 bits wide
  deslocamento deslocamento_1 (.in_1(in_1), .out_2(deslocamento_1_out_2));
  deslocamento_para_direita deslocamento_para_direita_1 (.in_1(in_1), .out_2(deslocamento_para_direita_1_out_2));
  somador somador_1 (.A(in_1), .B(in_2), .Cout(out_7), .Cin(in_4), .Q(somador_1_q));
  \subtração_de_8bits  \subtração_de_8bits_1  (
    .A(in_1), .B(in_2), .S(\subtração_de_8bits_1_s ), .in_3(in_5), .borrowout(out_8));
  mux_16_1 mux_16_1_1 (
    .in_1(and_1_out), .in_2(or_1_out), .in_3(not_1_out), .in_4(nor_1_out), .in_5(nand_1_out),
    .in_6(xor_1_out), .in_7(deslocamento_1_out_2), .in_8(deslocamento_para_direita_1_out_2), .out_18(out_6),
    .in_9(in_3), .in_10(somador_1_q), .in_11(\subtração_de_8bits_1_s ), .in_12({8{1'b0}}), .in_13({8{1'b0}}),
    .in_14({8{1'b0}}), .in_15({8{1'b0}}), .in_16({8{1'b0}}), .in_17({8{1'b0}}));
endmodule

// MUX
module mux_16_1 (
  input  [7:0] in_1,
  input  [7:0] in_2,
  input  [7:0] in_3,
  input  [7:0] in_4,
  input  [7:0] in_5,
  input  [7:0] in_6,
  input  [7:0] in_7,
  input  [7:0] in_8,
  input  [3:0] in_9,
  input  [7:0] in_10,
  input  [7:0] in_11,
  input  [7:0] in_12,
  input  [7:0] in_13,
  input  [7:0] in_14,
  input  [7:0] in_15,
  input  [7:0] in_16,
  input  [7:0] in_17,
  output [7:0] out_18
);

  wire [7:0] mux_8x1_8_bits_1_out_10, mux_8x1_8_bits_2_out_10;

  mux_8x1_8_bits mux_8x1_8_bits_1 (
    .in_1(in_1), .in_2(in_2), .in_3(in_3), .in_4(in_4), .in_5(in_9[2:0]), .in_6(in_5), .in_7(in_6),
    .in_8(in_7), .in_9(in_8), .out_10(mux_8x1_8_bits_1_out_10));
  mux_8x1_8_bits mux_8x1_8_bits_2 (
    .in_1(in_10), .in_2(in_11), .in_3(in_12), .in_4(in_13), .in_5(in_9[2:0]), .in_6(in_14), .in_7(in_15),
    .in_8(in_16), .in_9(in_17), .out_10(mux_8x1_8_bits_2_out_10));
  mux_2x1_8_bits mux_2x1_8_bits_1 (
    .E1(mux_8x1_8_bits_2_out_10), .E0(mux_8x1_8_bits_1_out_10), .S(in_9[3]), .out_4(out_18));
endmodule

module deslocamento (
  input  [7:0] in_1,
  output [7:0] out_2
);

  wire and_1_out, and_3_out, and_4_out, and_5_out, and_6_out, and_7_out, and_8_out, and_9_out, and_10_out,
       and_11_out, and_12_out, and_14_out, not_1_out;

  not not_1 (not_1_out, 1'b0);
  and and_1 (and_1_out, in_1[7], not_1_out);
  and and_2 (out_2[7], 1'b0, in_1[6]);
  and and_3 (and_3_out, in_1[6], not_1_out);
  and and_4 (and_4_out, 1'b0, in_1[5]);
  and and_5 (and_5_out, in_1[5], not_1_out);
  and and_6 (and_6_out, 1'b0, in_1[4]);
  and and_7 (and_7_out, in_1[4], not_1_out);
  and and_8 (and_8_out, 1'b0, in_1[3]);
  and and_9 (and_9_out, in_1[3], not_1_out);
  and and_10 (and_10_out, 1'b0, in_1[2]);
  and and_11 (and_11_out, in_1[2], not_1_out);
  and and_12 (and_12_out, 1'b0, in_1[1]);
  and and_13 (out_2[0], in_1[1], not_1_out);
  and and_14 (and_14_out, in_1[0], 1'b0);
  or S6 (out_2[6], and_1_out, and_4_out);
  or S5 (out_2[5], and_3_out, and_6_out);
  or S4 (out_2[4], and_5_out, and_8_out);
  or S3 (out_2[3], and_7_out, and_10_out);
  or S2 (out_2[2], and_9_out, and_12_out);
  or S1 (out_2[1], and_11_out, and_14_out);
endmodule

// Sub
module \subtração  (
  input  A,
  input  B,
  input  Cin,
  output sub,
  output borrowout
);

  wire and_1_out, and_2_out, and_3_out, and_4_out, and_5_out, and_6_out, and_7_out, not_1_out, not_2_out,
       not_3_out, not_4_out, not_5_out, not_6_out, not_7_out, not_8_out;

  not not_1 (not_1_out, A);
  not not_2 (not_2_out, B);
  not not_3 (not_3_out, A);
  not not_4 (not_4_out, Cin);
  not not_5 (not_5_out, B);
  not not_6 (not_6_out, Cin);
  not not_7 (not_7_out, A);
  not not_8 (not_8_out, A);
  and and_1 (and_1_out, not_1_out, not_2_out, Cin);
  and and_2 (and_2_out, not_3_out, B, not_4_out);
  and and_3 (and_3_out, A, not_5_out, not_6_out);
  and and_4 (and_4_out, A, B, Cin);
  and and_5 (and_5_out, not_7_out, Cin);
  and and_6 (and_6_out, not_8_out, B);
  and and_7 (and_7_out, B, Cin);
  or or_1 (sub, and_1_out, and_2_out, and_3_out, and_4_out);
  or or_2 (borrowout, and_5_out, and_6_out, and_7_out);
endmodule

// MUX
module mux_4x1_8_bits (
  input  [7:0] in_1,
  input  [7:0] in_2,
  input  [7:0] in_3,
  input  [7:0] in_4,
  input  [1:0] in_5,
  output [7:0] S
);

  wire [7:0] mux_2x1_8_bits_1_out_4, mux_2x1_8_bits_2_out_4;

  mux_2x1_8_bits mux_2x1_8_bits_1 (.E1(in_4), .E0(in_3), .S(in_5[0]), .out_4(mux_2x1_8_bits_1_out_4));
  mux_2x1_8_bits mux_2x1_8_bits_2 (.E1(in_2), .E0(in_1), .S(in_5[0]), .out_4(mux_2x1_8_bits_2_out_4));
  mux_2x1_8_bits mux_2x1_8_bits_3 (.E1(mux_2x1_8_bits_1_out_4), .E0(mux_2x1_8_bits_2_out_4), .S(in_5[1]), .out_4(S));
endmodule

// MUX
module mux_2x1_8_bits (
  input  [7:0] E0,
  input  [7:0] E1,
  input  S,
  output [7:0] out_4
);

  wire and_1_out, and_2_out, and_3_out, and_4_out, and_5_out, and_6_out, and_7_out, and_8_out, and_9_out,
       and_10_out, and_11_out, and_12_out, and_13_out, and_14_out, and_15_out, and_16_out, not_1_out,
       not_2_out, not_3_out, not_4_out, not_5_out, not_6_out, not_7_out, not_8_out;

  not not_1 (not_1_out, S);
  not not_2 (not_2_out, S);
  not not_3 (not_3_out, S);
  not not_4 (not_4_out, S);
  not not_5 (not_5_out, S);
  and and_1 (and_1_out, E1[7], S);
  and and_2 (and_2_out, E0[6], not_1_out);
  and and_3 (and_3_out, E1[6], S);
  and and_4 (and_4_out, E0[5], not_2_out);
  and and_5 (and_5_out, E1[5], S);
  and and_6 (and_6_out, E0[4], not_3_out);
  and and_7 (and_7_out, E1[4], S);
  and and_8 (and_8_out, E0[3], not_4_out);
  and and_9 (and_9_out, E1[3], S);
  and and_10 (and_10_out, E0[7], not_5_out);
  or or_1 (out_4[7], and_10_out, and_1_out);
  or or_2 (out_4[6], and_2_out, and_3_out);
  or or_3 (out_4[5], and_4_out, and_5_out);
  or or_4 (out_4[4], and_6_out, and_7_out);
  or or_5 (out_4[3], and_8_out, and_9_out);
  not not_6 (not_6_out, S);
  not not_7 (not_7_out, S);
  not not_8 (not_8_out, S);
  and and_11 (and_11_out, E0[0], not_6_out);
  and and_12 (and_12_out, E1[0], S);
  and and_13 (and_13_out, E0[1], not_7_out);
  and and_14 (and_14_out, E1[1], S);
  and and_15 (and_15_out, E0[2], not_8_out);
  and and_16 (and_16_out, E1[2], S);
  or or_6 (out_4[0], and_11_out, and_12_out);
  or or_7 (out_4[1], and_13_out, and_14_out);
  or or_8 (out_4[2], and_15_out, and_16_out);
endmodule

// MUX
module mux_8x1_8_bits (
  input  [7:0] in_1,
  input  [7:0] in_2,
  input  [7:0] in_3,
  input  [7:0] in_4,
  input  [2:0] in_5,
  input  [7:0] in_6,
  input  [7:0] in_7,
  input  [7:0] in_8,
  input  [7:0] in_9,
  output [7:0] out_10
);

  wire [7:0] mux_4x1_8_bits_1_s, mux_4x1_8_bits_2_s;

  mux_4x1_8_bits mux_4x1_8_bits_1 (
    .in_1(in_1), .in_2(in_2), .in_3(in_3), .in_4(in_4), .in_5(in_5[1:0]), .S(mux_4x1_8_bits_1_s));
  mux_4x1_8_bits mux_4x1_8_bits_2 (
    .in_1(in_6), .in_2(in_7), .in_3(in_8), .in_4(in_9), .in_5(in_5[1:0]), .S(mux_4x1_8_bits_2_s));
  mux_2x1_8_bits mux_2x1_8_bits_1 (.E1(mux_4x1_8_bits_2_s), .E0(mux_4x1_8_bits_1_s), .S(in_5[2]), .out_4(out_10));
endmodule

module somador (
  input  [7:0] A,
  input  [7:0] B,
  output Cout,
  output Cin,
  output [7:0] Q
);

  wire and_1_out, and_2_out, and_3_out, and_4_out, and_5_out, and_6_out, and_7_out, and_8_out, and_9_out,
       and_10_out, and_11_out, and_12_out, and_13_out, and_14_out, and_15_out, and_16_out, or_1_out,
       or_2_out, or_3_out, or_4_out, or_5_out, or_6_out, xor_1_out, xor_2_out, xor_3_out, xor_7_out,
       xor_8_out, xor_9_out, xor_13_out, xor_14_out;

  xor xor_1 (xor_1_out, A[0], B[0]);
  and and_1 (and_1_out, A[0], B[0]);
  xor xor_2 (xor_2_out, A[1], B[1]);
  and and_2 (and_2_out, A[1], B[1]);
  and and_3 (and_3_out, A[2], B[2]);
  xor xor_3 (xor_3_out, A[2], B[2]);
  xor xor_4 (Q[0], xor_1_out, 1'b0);
  and and_4 (and_4_out, xor_1_out, 1'b0);
  xor xor_5 (Q[1], xor_2_out, or_1_out);
  and and_5 (and_5_out, xor_2_out, or_1_out);
  xor xor_6 (Q[2], xor_3_out, or_2_out);
  and and_6 (and_6_out, xor_3_out, or_2_out);
  or or_1 (or_1_out, and_4_out, and_1_out);
  or or_2 (or_2_out, and_5_out, and_2_out);
  or or_3 (or_3_out, and_6_out, and_3_out);
  xor xor_7 (xor_7_out, A[5], B[5]);
  and and_7 (and_7_out, A[5], B[5]);
  xor xor_8 (xor_8_out, A[4], B[4]);
  and and_8 (and_8_out, A[4], B[4]);
  xor xor_9 (xor_9_out, A[3], B[3]);
  and and_9 (and_9_out, A[3], B[3]);
  xor xor_10 (Q[5], xor_7_out, or_5_out);
  and and_10 (and_10_out, xor_7_out, or_5_out);
  xor xor_11 (Q[4], xor_8_out, or_6_out);
  and and_11 (and_11_out, xor_8_out, or_6_out);
  xor xor_12 (Q[3], xor_9_out, or_3_out);
  and and_12 (and_12_out, xor_9_out, or_3_out);
  or or_4 (or_4_out, and_10_out, and_7_out);
  or or_5 (or_5_out, and_11_out, and_8_out);
  or or_6 (or_6_out, and_12_out, and_9_out);
  xor xor_13 (xor_13_out, A[6], B[6]);
  and and_13 (and_13_out, A[6], B[6]);
  xor xor_14 (xor_14_out, A[7], B[7]);
  and and_14 (and_14_out, A[7], B[7]);
  xor xor_15 (Q[6], xor_13_out, or_4_out);
  and and_15 (and_15_out, xor_13_out, or_4_out);
  xor xor_16 (Q[7], xor_14_out, Cout);
  and and_16 (and_16_out, xor_14_out, Cout);
  or or_7 (Cout, and_15_out, and_13_out);
  or or_8 (Cin, and_16_out, and_14_out);
endmodule

module \subtração_de_8bits  (
  input  [7:0] A,
  input  [7:0] B,
  input  in_3,
  output borrowout,
  output [7:0] S
);

  wire \subtração_2_borrowout , \subtração_3_borrowout , \subtração_4_borrowout , \subtração_5_borrowout ,
       \subtração_6_borrowout , \subtração_7_borrowout , \subtração_8_borrowout ;

  \subtração  \subtração_1  (.Cin(\subtração_2_borrowout ), .sub(S[7]), .borrowout(borrowout), .A(A[7]), .B(B[7]));
  \subtração  \subtração_2  (
    .Cin(\subtração_3_borrowout ), .sub(S[6]), .borrowout(\subtração_2_borrowout ), .A(A[6]), .B(B[6]));
  \subtração  \subtração_3  (
    .Cin(\subtração_4_borrowout ), .sub(S[5]), .borrowout(\subtração_3_borrowout ), .A(A[5]), .B(B[5]));
  \subtração  \subtração_4  (
    .Cin(\subtração_5_borrowout ), .sub(S[4]), .borrowout(\subtração_4_borrowout ), .A(A[4]), .B(B[4]));
  \subtração  \subtração_5  (
    .Cin(\subtração_6_borrowout ), .sub(S[3]), .borrowout(\subtração_5_borrowout ), .A(A[3]), .B(B[3]));
  \subtração  \subtração_6  (
    .Cin(\subtração_7_borrowout ), .sub(S[2]), .borrowout(\subtração_6_borrowout ), .A(A[2]), .B(B[2]));
  \subtração  \subtração_7  (
    .Cin(\subtração_8_borrowout ), .sub(S[1]), .borrowout(\subtração_7_borrowout ), .A(A[1]), .B(B[1]));
  \subtração  \subtração_8  (.Cin(in_3), .sub(S[0]), .borrowout(\subtração_8_borrowout ), .A(A[0]), .B(B[0]));
endmodule

module deslocamento_para_direita (
  input  [7:0] in_1,
  output [7:0] out_2
);

  wire and_1_out, and_3_out, and_4_out, and_5_out, and_6_out, and_7_out, and_8_out, and_9_out, and_10_out,
       and_11_out, and_12_out, and_14_out, not_1_out;

  not not_1 (not_1_out, 1'b1);
  and and_1 (and_1_out, in_1[7], not_1_out);
  and and_2 (out_2[7], 1'b1, in_1[6]);
  and and_3 (and_3_out, in_1[6], not_1_out);
  and and_4 (and_4_out, 1'b1, in_1[5]);
  and and_5 (and_5_out, in_1[5], not_1_out);
  and and_6 (and_6_out, 1'b1, in_1[4]);
  and and_7 (and_7_out, in_1[4], not_1_out);
  and and_8 (and_8_out, 1'b1, in_1[3]);
  and and_9 (and_9_out, in_1[3], not_1_out);
  and and_10 (and_10_out, 1'b1, in_1[2]);
  and and_11 (and_11_out, in_1[2], not_1_out);
  and and_12 (and_12_out, 1'b1, in_1[1]);
  and and_13 (out_2[0], in_1[1], not_1_out);
  and and_14 (and_14_out, in_1[0], 1'b1);
  or S6 (out_2[6], and_1_out, and_4_out);
  or S5 (out_2[5], and_3_out, and_6_out);
  or S4 (out_2[4], and_5_out, and_8_out);
  or S3 (out_2[3], and_7_out, and_10_out);
  or S2 (out_2[2], and_9_out, and_12_out);
  or S1 (out_2[1], and_11_out, and_14_out);
endmodule
