// Logisim project 12-MaquinaDeEstado.circ as structural Verilog: 2 circuits, main circuit main
module main (
  input  P,
  input  ENTRA,
  input  C,
  output SAI
);

  wire and_1_out, clock_1_out, jk_d_1_q, not_1_out;

  Clock clock_1 (.out(clock_1_out));
  and and_1 (and_1_out, ENTRA, not_1_out);
  jk_d jk_d_1 (.P(P), .D(and_1_out), .CLK(clock_1_out), .C(C), .Q(jk_d_1_q));  // open: N
  not not_1 (not_1_out, SAI);
  and and_2 (SAI, jk_d_1_q, ENTRA);
endmodule

module jk_d (
  input  P,
  input  D,
  input  CLK,
  input  C,
  output Q,
  output N
);

  wire nand_1_out, nand_2_out, nand_3_out, nand_4_out, nand_5_out, nand_6_out, not_1_out, not_2_out;

  not not_1 (not_1_out, D);
  not not_2 (not_2_out, CLK);
  nand nand_1 (nand_1_out, D, CLK, N);
  nand nand_2 (nand_2_out, not_1_out, Q, CLK);
  nand nand_3 (nand_3_out, P, nand_4_out, nand_1_out);
  nand nand_4 (nand_4_out, nand_3_out, C, nand_2_out);
  nand nand_5 (nand_5_out, nand_3_out, not_2_out);
  nand nand_6 (nand_6_out, nand_4_out, not_2_out);
  nand nand_7 (Q, P, N, nand_5_out);
  nand nand_8 (N, nand_6_out, nand_6_out, Q, C);
endmodule
