// Logisim project 14-detector_paridade_ímpar.circ as structural Verilog: 1 circuit, main circuit detector_paridade_ímpar
module \detector_paridade_ímpar  (
  input  [3:0] Entrada,
  output S
);

  wire and_1_out, and_2_out, and_3_out, and_4_out, and_5_out, and_6_out, and_7_out, and_8_out, not_1_out,
       not_2_out, not_3_out, not_4_out, not_5_out, not_6_out, not_7_out, not_8_out, not_9_out, not_10_out,
       not_11_out, not_12_out, not_13_out, not_14_out, not_15_out, not_16_out;

  not not_1 (not_1_out, Entrada[0]);
  and and_1 (and_1_out, Entrada[3], Entrada[2], Entrada[1], not_1_out);
  not not_2 (not_2_out, Entrada[2]);
  not not_3 (not_3_out, Entrada[1]);
  and and_2 (and_2_out, Entrada[3], Entrada[2], not_3_out, Entrada[0]);
  not not_4 (not_4_out, Entrada[3]);
  and and_3 (and_3_out, not_4_out, Entrada[2], Entrada[1], Entrada[0]);
  and and_4 (and_4_out, Entrada[3], not_2_out, Entrada[1], Entrada[0]);
  not not_5 (not_5_out, Entrada[1]);
  not not_6 (not_6_out, Entrada[2]);
  and and_5 (and_5_out, Entrada[3], not_6_out, not_5_out, not_10_out);
  not not_7 (not_7_out, Entrada[0]);
  not not_8 (not_8_out, Entrada[3]);
  not not_9 (not_9_out, Entrada[1]);
  not not_10 (not_10_out, Entrada[0]);
  and and_6 (and_6_out, not_8_out, Entrada[2], not_9_out, not_7_out);
  not not_11 (not_11_out, Entrada[3]);
  not not_12 (not_12_out, Entrada[0]);
  not not_13 (not_13_out, Entrada[2]);
  and and_7 (and_7_out, not_11_out, not_13_out, Entrada[1], not_12_out);
  not not_14 (not_14_out, Entrada[3]);
  not not_15 (not_15_out, Entrada[1]);
  not not_16 (not_16_out, Entrada[2]);
  and and_8 (and_8_out, not_14_out, not_16_out, not_15_out, Entrada[0]);
  or or_1 (S, and_8_out, and_7_out, and_6_out, and_5_out, and_3_out, and_4_out, and_2_out, and_1_out);
endmodule
