// Logisim project 15-Resolva um problema de otimizaç╞o lógica utilizando mapas de Karnaugh e.circ as structural Verilog: 1 circuit, main circuit main
module main (
  input  A,
  input  B,
  input  C,
  input  A_2,
  input  B_2,
  input  C_2,
  output out_7,
  output out_8
);

  wire and_1_out, and_2_out, and_3_out, and_4_out, and_5_out, and_6_out, not_1_out, not_2_out, not_3_out,
       not_4_out, not_5_out, not_6_out, not_7_out, not_8_out, not_9_out;

  and and_1 (and_1_out, A, B, C);
  not not_1 (not_1_out, A_2);
  not not_2 (not_2_out, B_2);
  not not_3 (not_3_out, B);
  and and_2 (and_2_out, A, not_3_out, C);
  and and_3 (and_3_out, not_1_out, not_2_out);
  not not_4 (not_4_out, A);
  or or_1 (out_8, and_3_out, C_2);
  not not_5 (not_5_out, A);
  and and_4 (and_4_out, not_4_out, B, C);
  or or_2 (out_7, and_1_out, and_2_out, and_4_out, and_5_out, and_6_out);
  not not_6 (not_6_out, B);
  and and_5 (and_5_out, not_5_out, not_6_out, C);
  not not_7 (not_7_out, B);
  not not_8 (not_8_out, C);
  not not_9 (not_9_out, A);
  and and_6 (and_6_out, not_9_out, not_7_out, not_8_out);
endmodule
