// Logisim project 2-Multiplexador de quatro entrada.circ as structural Verilog: 1 circuit, main circuit main
module main (
  input  E0,
  input  E1,
  input  E2,
  input  E3,
  input  in_5,
  input  in_6,
  output out_7
);

  wire and_1_out, and_2_out, and_3_out, and_4_out, not_1_out, not_2_out, not_3_out, not_4_out;

  not not_1 (not_1_out, in_5);
  not not_2 (not_2_out, in_6);
  not not_3 (not_3_out, in_5);
  not not_4 (not_4_out, in_6);
  and and_1 (and_1_out, E0, not_1_out, not_2_out);
  and and_2 (and_2_out, E1, not_3_out, in_6);
  and and_3 (and_3_out, E2, in_5, not_4_out);
  and and_4 (and_4_out, E3, in_5, in_6);
  or or_1 (out_7, and_1_out, and_2_out, and_3_out, and_4_out);
endmodule
