// Logisim project 4-Somador de 8 bits que recebe um valor inteiro e soma com o valor 4.circ as structural Verilog: 3 circuits, main circuit Somador 8bits
// Somador 8x1
module Somador_8bits (
  input  a0,
  input  a5,
  input  a6,
  input  b0,
  input  b5,
  input  b6,
  input  a1,
  input  a4,
  input  a7,
  input  b1,
  input  b4,
  input  b7,
  input  a2,
  input  a3,
  input  b2,
  input  b3,
  output Cout,
  output Cin,
  output [7:0] Q
);

  wire and_1_out, and_2_out, and_3_out, and_4_out, and_5_out, and_6_out, and_7_out, and_8_out, and_9_out,
       and_10_out, and_11_out, and_12_out, and_13_out, and_14_out, and_15_out, and_16_out, or_1_out,
       or_2_out, or_3_out, or_4_out, or_5_out, or_6_out, xor_1_out, xor_2_out, xor_3_out, xor_7_out,
       xor_8_out, xor_9_out, xor_13_out, xor_14_out;

  xor xor_1 (xor_1_out, a0, b0);
  and and_1 (and_1_out, a0, b0);
  xor xor_2 (xor_2_out, a1, b1);
  and and_2 (and_2_out, a1, b1);
  xor xor_3 (xor_3_out, a2, b2);
  and and_3 (and_3_out, a2, b2);
  xor xor_4 (Q[0], xor_1_out, 1'b0);
  and and_4 (and_4_out, xor_1_out, 1'b0);
  xor xor_5 (Q[1], xor_2_out, or_1_out);
  and and_5 (and_5_out, xor_2_out, or_1_out);
  xor xor_6 (Q[2], xor_3_out, or_2_out);
  and and_6 (and_6_out, xor_3_out, or_2_out);
  or or_1 (or_1_out, and_4_out, and_1_out);
  or or_2 (or_2_out, and_5_out, and_2_out);
  or or_3 (or_3_out, and_6_out, and_3_out);
  xor xor_7 (xor_7_out, a5, b5);
  and and_7 (and_7_out, a5, b5);
  xor xor_8 (xor_8_out, a4, b4);
  and and_8 (and_8_out, a4, b4);
  xor xor_9 (xor_9_out, a3, b3);
  and and_9 (and_9_out, a3, b3);
  xor xor_10 (Q[5], xor_7_out, or_5_out);
  and and_10 (and_10_out, xor_7_out, or_5_out);
  xor xor_11 (Q[4], xor_8_out, or_6_out);
  and and_11 (and_11_out, xor_8_out, or_6_out);
  or or_4 (or_4_out, and_10_out, and_7_out);
  or or_5 (or_5_out, and_11_out, and_8_out);
  xor xor_12 (Q[3], xor_9_out, or_3_out);
  and and_12 (and_12_out, xor_9_out, or_3_out);
  or or_6 (or_6_out, and_12_out, and_9_out);
  xor xor_13 (xor_13_out, a6, b6);
  and and_13 (and_13_out, a6, b6);
  xor xor_14 (xor_14_out, a7, b7);
  and and_14 (and_14_out, a7, b7);
  xor xor_15 (Q[6], xor_13_out, or_4_out);
  and and_15 (and_15_out, xor_13_out, or_4_out);
  xor xor_16 (Q[7], xor_14_out, Cout);
  and and_16 (and_16_out, xor_14_out, Cout);
  or or_7 (Cout, and_15_out, and_13_out);
  or or_8 (Cin, and_16_out, and_14_out);
endmodule

module entrada_de_um_numero_inteiro_somando_com_mais_4 (
  input  [7:0] in_1,
  output [7:0] out_2
);

  Somador_8bits somador_8bits_1 (
    .a0(1'b0), .a5(1'b0), .a6(1'b0), .b0(in_1[0]), .b5(in_1[5]), .b6(in_1[6]), .a1(1'b0), .a4(1'b0),
    .a7(1'b0), .b1(in_1[1]), .b4(in_1[4]), .b7(in_1[7]), .a2(1'b1), .a3(1'b0), .b2(in_1[2]), .b3(in_1[3]),
    .Q(out_2));  // open: Cin, Cout
endmodule

module a (
  input  [7:0] A,
  input  [7:0] B,
  output Cout,
  output Cin,
  output [7:0] Q
);

  wire and_1_out, and_2_out, and_3_out, and_4_out, and_5_out, and_6_out, and_7_out, and_8_out, and_9_out,
       and_10_out, and_11_out, and_12_out, and_13_out, and_14_out, and_15_out, and_16_out, or_1_out,
       or_2_out, or_3_out, or_4_out, or_5_out, or_6_out, xor_1_out, xor_2_out, xor_3_out, xor_7_out,
       xor_8_out, xor_9_out, xor_13_out, xor_14_out;

  xor xor_1 (xor_1_out, A[0], B[0]);
  and and_1 (and_1_out, A[0], B[0]);
  xor xor_2 (xor_2_out, A[1], B[1]);
  and and_2 (and_2_out, A[1], B[1]);
  and and_3 (and_3_out, A[2], B[2]);
  xor xor_3 (xor_3_out, A[2], B[2]);
  xor xor_4 (Q[0], xor_1_out, 1'b0);
  and and_4 (and_4_out, xor_1_out, 1'b0);
  xor xor_5 (Q[1], xor_2_out, or_1_out);
  and and_5 (and_5_out, xor_2_out, or_1_out);
  xor xor_6 (Q[2], xor_3_out, or_2_out);
  and and_6 (and_6_out, xor_3_out, or_2_out);
  or or_1 (or_1_out, and_4_out, and_1_out);
  or or_2 (or_2_out, and_5_out, and_2_out);
  or or_3 (or_3_out, and_6_out, and_3_out);
  xor xor_7 (xor_7_out, A[5], B[5]);
  and and_7 (and_7_out, A[5], B[5]);
  xor xor_8 (xor_8_out, A[4], B[4]);
  and and_8 (and_8_out, A[4], B[4]);
  xor xor_9 (xor_9_out, A[3], B[3]);
  and and_9 (and_9_out, A[3], B[3]);
  xor xor_10 (Q[5], xor_7_out, or_5_out);
  and and_10 (and_10_out, xor_7_out, or_5_out);
  xor xor_11 (Q[4], xor_8_out, or_6_out);
  and and_11 (and_11_out, xor_8_out, or_6_out);
  xor xor_12 (Q[3], xor_9_out, or_3_out);
  and and_12 (and_12_out, xor_9_out, or_3_out);
  or or_4 (or_4_out, and_10_out, and_7_out);
  or or_5 (or_5_out, and_11_out, and_8_out);
  or or_6 (or_6_out, and_12_out, and_9_out);
  xor xor_13 (xor_13_out, A[6], B[6]);
  and and_13 (and_13_out, A[6], B[6]);
  xor xor_14 (xor_14_out, A[7], B[7]);
  and and_14 (and_14_out, A[7], B[7]);
  xor xor_15 (Q[6], xor_13_out, or_4_out);
  and and_15 (and_15_out, xor_13_out, or_4_out);
  xor xor_16 (Q[7], xor_14_out, Cout);
  and and_16 (and_16_out, xor_14_out, Cout);
  or or_7 (Cout, and_15_out, and_13_out);
  or or_8 (Cin, and_16_out, and_14_out);
endmodule
