// Logisim project 8-Somador 8bits.circ as structural Verilog: 1 circuit, main circuit Somador 8bits
module Somador_8bits (
  input  in_1,
  input  in_2,
  input  in_3,
  input  in_4,
  input  in_5,
  input  in_6,
  input  in_7,
  input  in_8,
  input  in_9,
  input  in_10,
  input  in_11,
  input  in_12,
  input  in_13,
  input  in_14,
  input  in_15,
  input  in_16,
  output out_17,
  output out_18,
  output out_19,
  output out_20,
  output out_21,
  output out_22,
  output out_23,
  output out_24,
  output out_25,
  output out_26,
  output out_27,
  output out_28,
  output out_29,
  output out_30,
  output [7:0] out_31,
  output out_32,
  output out_33
);

  wire and_1_out, and_2_out, and_3_out, and_4_out, and_5_out, and_6_out, and_7_out, and_8_out, and_9_out,
       and_10_out, and_11_out, and_12_out, and_13_out, and_14_out, and_15_out, and_16_out, xor_1_out,
       xor_2_out, xor_3_out, xor_7_out, xor_8_out, xor_9_out, xor_13_out, xor_14_out;

  xor xor_1 (xor_1_out, in_1, in_4);
  and and_1 (and_1_out, in_1, in_4);
  xor xor_2 (xor_2_out, in_7, in_10);
  and and_2 (and_2_out, in_7, in_10);
  xor xor_3 (xor_3_out, in_13, in_15);
  and and_3 (and_3_out, in_13, in_15);
  xor xor_4 (out_17, xor_1_out, 1'b0);
  and and_4 (and_4_out, xor_1_out, 1'b0);
  xor xor_5 (out_23, xor_2_out, out_20);
  and and_5 (and_5_out, xor_2_out, out_20);
  xor xor_6 (out_29, xor_3_out, out_26);
  and and_6 (and_6_out, xor_3_out, out_26);
  or or_1 (out_20, and_4_out, and_1_out);
  or or_2 (out_26, and_5_out, and_2_out);
  or or_3 (out_32, and_6_out, and_3_out);
  xor xor_7 (xor_7_out, in_2, in_5);
  and and_7 (and_7_out, in_2, in_5);
  xor xor_8 (xor_8_out, in_8, in_11);
  and and_8 (and_8_out, in_8, in_11);
  xor xor_9 (xor_9_out, in_14, in_16);
  and and_9 (and_9_out, in_14, in_16);
  xor xor_10 (out_18, xor_7_out, out_27);
  and and_10 (and_10_out, xor_7_out, out_27);
  xor xor_11 (out_24, xor_8_out, out_33);
  and and_11 (and_11_out, xor_8_out, out_33);
  or or_4 (out_21, and_10_out, and_7_out);
  or or_5 (out_27, and_11_out, and_8_out);
  xor xor_12 (out_30, xor_9_out, out_32);
  and and_12 (and_12_out, xor_9_out, out_32);
  or or_6 (out_33, and_12_out, and_9_out);
  xor xor_13 (xor_13_out, in_3, in_6);
  and and_13 (and_13_out, in_3, in_6);
  xor xor_14 (xor_14_out, in_9, in_12);
  and and_14 (and_14_out, in_9, in_12);
  xor xor_15 (out_19, xor_13_out, out_21);
  and and_15 (and_15_out, xor_13_out, out_21);
  xor xor_16 (out_25, xor_14_out, out_22);
  and and_16 (and_16_out, xor_14_out, out_22);
  or or_7 (out_22, and_15_out, and_13_out);
  or or_8 (out_28, and_16_out, and_14_out);

  assign out_31 = {out_25, out_19, out_18, out_24, out_30, out_29, out_23, out_17};
endmodule
