// Logisim project Decodificador_Enderecos_Parte1.circ as structural Verilog: 1 circuit, main circuit Decodificador_Enderecos
module Decodificador_Enderecos (
  input  [5:0] ENDERECO,
  output [3:0] A3_A0,
  output A5,
  output out_4,
  output A4,
  output out_6,
  output out_7,
  output out_8
);

  wire not_1_out, not_2_out;

  not not_1 (not_1_out, ENDERECO[5]);
  not not_2 (not_2_out, ENDERECO[4]);
  and PORTA1_CSROM (out_4, not_1_out, not_2_out);
  and PORTA2_CS_RAM (out_6, not_1_out, ENDERECO[4]);
  and PORTA3_CS_REG (out_7, ENDERECO[5], not_2_out);
  and PORTA4_CS_IO (out_8, ENDERECO[5], ENDERECO[4]);

  assign A3_A0 = ENDERECO[3:0];
  assign A4 = ENDERECO[4];
  assign A5 = ENDERECO[5];
endmodule
