// Logisim project parte2_cabeada.circ as structural Verilog
// D2
module Unidade_Controle_Cabeada (
  input  CLOCK,
  input  RESET,
  input  [5:0] OPCODE,
  output PCWr,
  output MemRd,
  output IRWr,
  output SrcB_0,
  output RegWr,
  output SrcA,
  output PCWrC,
  output PCSrc,
  output ALUOp_0,
  output ALUOp_1,
  output SrcB_1
);

  wire D0_out, D1_1_out, D1_out, D2_out, not_1_out, or_1_out, Q0_qn, Q1_qn, Q2_qn;

  not not_1 (not_1_out, OPCODE[2]);
  D_Flip_Flop Q2 (.D(D2_out), .clk(CLOCK), .Q(ALUOp_0), .Qn(Q2_qn), .reset(RESET));  // open: preset
  and D2 (D2_out, OPCODE[2], Q1_qn, SrcB_1);
  and D1_1 (D1_1_out, ALUOp_1, Q0_qn);
  and D1 (D1_out, not_1_out, Q1_qn, SrcB_1);
  and D0 (D0_out, Q2_qn, Q0_qn);
  D_Flip_Flop Q1 (.D(or_1_out), .clk(CLOCK), .Q(ALUOp_1), .Qn(Q1_qn), .reset(RESET));  // open: preset
  or or_1 (or_1_out, D1_1_out, D1_out);
  and and_1 (IRWr, Q2_qn, Q1_qn, Q0_qn);
  and and_2 (RegWr, ALUOp_1, SrcB_1);
  D_Flip_Flop Q0 (.D(D0_out), .clk(CLOCK), .Q(SrcB_1), .Qn(Q0_qn), .reset(RESET));  // open: preset
  or or_2 (SrcA, ALUOp_1, ALUOp_0);
  Hex_Digit_Display hex_digit_display_1 (.value({1'b0, ALUOp_0, ALUOp_1, SrcB_1}));  // open: dp

  assign MemRd = IRWr;
  assign PCSrc = ALUOp_0;
  assign PCWr = IRWr;
  assign PCWrC = ALUOp_0;
  assign SrcB_0 = IRWr;
endmodule

module Registrador_FLIP_FLOP_D_661eac99 (
  input  CLK,
  input  D,
  output Q,
  output Q_NEGADO
);

  wire and_1_out, and_2_out, not_1_out;

  not not_1 (not_1_out, D);
  and and_1 (and_1_out, not_1_out, CLK);
  and and_2 (and_2_out, CLK, D);
  nor nor_1 (Q, and_1_out, Q_NEGADO);
  nor nor_2 (Q_NEGADO, Q, and_2_out);
endmodule
