// Logisim project ram.circ as structural Verilog: 3 circuits, main circuit main
module main (
  input  [7:0] in_1,
  input  in_2,
  input  [3:0] in_3,
  output [7:0] out_4
);

  wire clock_1_out;

  Clock clock_1 (.out(clock_1_out));
  memoriaRAM16by memoriaram16by_1 (.D(in_1), .escrita(in_2), .endereco(in_3), .clock(clock_1_out), .saida(out_4));
endmodule

module registrador8bits (
  input  [7:0] in_1,
  input  we,
  input  clk,
  output [7:0] q
);

  wire [7:0] multiplexer_1_out;

  Multiplexer #(.width(8)) multiplexer_1 (.in0(q), .in1(in_1), .out(multiplexer_1_out), .sel(we));
  D_Flip_Flop d_ff_1 (.D(multiplexer_1_out[0]), .clk(clk), .Q(q[0]));  // open: Qn, preset, reset
  D_Flip_Flop d_ff_2 (.D(multiplexer_1_out[1]), .clk(clk), .Q(q[1]));  // open: Qn, preset, reset
  D_Flip_Flop d_ff_3 (.D(multiplexer_1_out[2]), .clk(clk), .Q(q[2]));  // open: Qn, preset, reset
  D_Flip_Flop d_ff_4 (.D(multiplexer_1_out[3]), .clk(clk), .Q(q[3]));  // open: Qn, preset, reset
  D_Flip_Flop d_ff_5 (.D(multiplexer_1_out[4]), .clk(clk), .Q(q[4]));  // open: Qn, preset, reset
  D_Flip_Flop d_ff_6 (.D(multiplexer_1_out[5]), .clk(clk), .Q(q[5]));  // open: Qn, preset, reset
  D_Flip_Flop d_ff_7 (.D(multiplexer_1_out[6]), .clk(clk), .Q(q[6]));  // open: Qn, preset, reset
  D_Flip_Flop d_ff_8 (.D(multiplexer_1_out[7]), .clk(clk), .Q(q[7]));  // open: Qn, preset, reset

  // Notes on the sheet:
  //   d
endmodule

module memoriaRAM16by (
  input  [7:0] D,
  input  escrita,
  input  [3:0] endereco,
  input  clock,
  output [7:0] saida
);

  wire and_1_out, and_2_out, and_3_out, and_4_out, and_5_out, and_6_out, and_7_out, and_8_out, and_9_out,
       and_10_out, and_11_out, and_12_out, and_13_out, and_14_out, and_15_out, and_16_out, decoder_1_out0,
       decoder_1_out1, decoder_1_out2, decoder_1_out3, decoder_1_out4, decoder_1_out5, decoder_1_out6,
       decoder_1_out7, decoder_1_out8, decoder_1_out9, decoder_1_out10, decoder_1_out11, decoder_1_out12,
       decoder_1_out13, decoder_1_out14, decoder_1_out15;
  wire [7:0] registrador8bits_1_q, registrador8bits_2_q, registrador8bits_3_q, registrador8bits_4_q,
       registrador8bits_5_q, registrador8bits_6_q, registrador8bits_7_q, registrador8bits_8_q,
       registrador8bits_9_q, registrador8bits_10_q, registrador8bits_11_q, registrador8bits_12_q,
       registrador8bits_13_q, registrador8bits_14_q, registrador8bits_15_q, registrador8bits_16_q;

  and and_1 (and_1_out, decoder_1_out0, escrita);
  and and_2 (and_2_out, decoder_1_out1, escrita);
  and and_3 (and_3_out, decoder_1_out2, escrita);
  and and_4 (and_4_out, decoder_1_out3, escrita);
  and and_5 (and_5_out, decoder_1_out4, escrita);
  and and_6 (and_6_out, decoder_1_out5, escrita);
  and and_7 (and_7_out, decoder_1_out6, escrita);
  and and_8 (and_8_out, decoder_1_out7, escrita);
  registrador8bits registrador8bits_1 (.in_1(D), .we(and_1_out), .clk(clock), .q(registrador8bits_1_q));
  registrador8bits registrador8bits_2 (.in_1(D), .we(and_2_out), .clk(clock), .q(registrador8bits_2_q));
  registrador8bits registrador8bits_3 (.in_1(D), .we(and_3_out), .clk(clock), .q(registrador8bits_3_q));
  registrador8bits registrador8bits_4 (.in_1(D), .we(and_4_out), .clk(clock), .q(registrador8bits_4_q));
  registrador8bits registrador8bits_5 (.in_1(D), .we(and_5_out), .clk(clock), .q(registrador8bits_5_q));
  registrador8bits registrador8bits_6 (.in_1(D), .we(and_6_out), .clk(clock), .q(registrador8bits_6_q));
  registrador8bits registrador8bits_7 (.in_1(D), .we(and_7_out), .clk(clock), .q(registrador8bits_7_q));
  registrador8bits registrador8bits_8 (.in_1(D), .we(and_8_out), .clk(clock), .q(registrador8bits_8_q));
  Decoder #(.select(4)) decoder_1 (
    .out0(decoder_1_out0), .out1(decoder_1_out1), .out2(decoder_1_out2), .out3(decoder_1_out3),
    .out4(decoder_1_out4), .out5(decoder_1_out5), .out6(decoder_1_out6), .out7(decoder_1_out7),
    .out8(decoder_1_out8), .out9(decoder_1_out9), .out10(decoder_1_out10), .out11(decoder_1_out11),
    .out12(decoder_1_out12), .out13(decoder_1_out13), .out14(decoder_1_out14), .out15(decoder_1_out15),
    .sel(endereco), .en(1'b1));
  and and_9 (and_9_out, decoder_1_out8, escrita);
  and and_10 (and_10_out, decoder_1_out9, escrita);
  and and_11 (and_11_out, decoder_1_out10, escrita);
  and and_12 (and_12_out, decoder_1_out11, escrita);
  and and_13 (and_13_out, decoder_1_out12, escrita);
  and and_14 (and_14_out, decoder_1_out13, escrita);
  and and_15 (and_15_out, decoder_1_out14, escrita);
  and and_16 (and_16_out, decoder_1_out15, escrita);
  registrador8bits registrador8bits_9 (.in_1(D), .we(and_9_out), .clk(clock), .q(registrador8bits_9_q));
  registrador8bits registrador8bits_10 (.in_1(D), .we(and_10_out), .clk(clock), .q(registrador8bits_10_q));
  registrador8bits registrador8bits_11 (.in_1(D), .we(and_12_out), .clk(clock), .q(registrador8bits_11_q));
  registrador8bits registrador8bits_12 (.in_1(D), .we(and_14_out), .clk(clock), .q(registrador8bits_12_q));
  registrador8bits registrador8bits_13 (.in_1(D), .we(and_11_out), .clk(clock), .q(registrador8bits_13_q));
  registrador8bits registrador8bits_14 (.in_1(D), .we(and_13_out), .clk(clock), .q(registrador8bits_14_q));
  registrador8bits registrador8bits_15 (.in_1(D), .we(and_15_out), .clk(clock), .q(registrador8bits_15_q));
  registrador8bits registrador8bits_16 (.in_1(D), .we(and_16_out), .clk(clock), .q(registrador8bits_16_q));
  Multiplexer #(.select(4), .width(8)) multiplexer_1 (
    .in0(registrador8bits_1_q), .in1(registrador8bits_2_q), .in2(registrador8bits_3_q),
    .in3(registrador8bits_4_q), .in4(registrador8bits_5_q), .in5(registrador8bits_6_q),
    .in6(registrador8bits_7_q), .in7(registrador8bits_8_q), .in8(registrador8bits_9_q),
    .in9(registrador8bits_10_q), .in10(registrador8bits_13_q), .in11(registrador8bits_11_q),
    .in12(registrador8bits_14_q), .in13(registrador8bits_12_q), .in14(registrador8bits_15_q),
    .in15(registrador8bits_16_q), .out(saida), .sel(endereco));

  // Notes on the sheet:
  //   ender
endmodule
