// Logisim project Decodificador_Enderecos_Parte1.circ as structural Verilog: 1 circuit, main circuit Decodificador_Enderecos
module Decodificador_Enderecos (
  input  [5:0] ENDERECO,
  output [3:0] A3_A0,
  output A5,
  output cs_rom,
  output A4,
  output cs_ram,
  output cs_reg,
  output cs_io
);

  wire not_1_out, not_2_out;

  not not_1 (not_1_out, ENDERECO[5]);
  not not_2 (not_2_out, ENDERECO[4]);
  and PORTA1_CSROM (cs_rom, not_1_out, not_2_out);
  and PORTA2_CS_RAM (cs_ram, not_1_out, ENDERECO[4]);
  and PORTA3_CS_REG (cs_reg, ENDERECO[5], not_2_out);
  and PORTA4_CS_IO (cs_io, ENDERECO[5], ENDERECO[4]);

  assign A3_A0 = ENDERECO[3:0];
  assign A4 = ENDERECO[4];
  assign A5 = ENDERECO[5];
endmodule
