// Logisim project SELECAO-DE-8-BITS.circ as structural Verilog: 2 circuits, main circuit MUX_1BIT
module MUX_1BIT (
  input  E0,
  input  E1,
  input  E2,
  input  E3,
  input  S1,
  input  S0,
  output Y
);

  wire and_1_out, and_2_out, and_3_out, and_4_out, not_1_out, not_2_out, not_3_out, not_4_out;

  not not_1 (not_1_out, S1);
  not not_2 (not_2_out, S0);
  not not_3 (not_3_out, S1);
  not not_4 (not_4_out, S0);
  and and_1 (and_1_out, E0, not_1_out, not_2_out);
  and and_2 (and_2_out, E1, not_3_out, S0);
  and and_3 (and_3_out, E2, S1, not_4_out);
  and and_4 (and_4_out, E3, S1, S0);
  or or_1 (Y, and_1_out, and_2_out, and_3_out, and_4_out);
endmodule

module MUXX_8BITS (
  input  S1,
  input  S0,
  input  [7:0] E0,
  input  [7:0] E1,
  input  [7:0] E2,
  input  [7:0] E3,
  output [7:0] Y
);

  MUX_1BIT mux_1bit_1 (.E0(E0[0]), .E1(E1[0]), .E2(E2[0]), .E3(E3[0]), .S1(S1), .S0(S0), .Y(Y[0]));
  MUX_1BIT mux_1bit_2 (.E0(E0[1]), .E1(E1[1]), .E2(E2[1]), .E3(E3[1]), .S1(S1), .S0(S0), .Y(Y[1]));
  MUX_1BIT mux_1bit_3 (.E0(E0[2]), .E1(E1[2]), .E2(E2[2]), .E3(E3[2]), .S1(S1), .S0(S0), .Y(Y[2]));
  MUX_1BIT mux_1bit_4 (.E0(E0[3]), .E1(E1[3]), .E2(E2[3]), .E3(E3[3]), .S1(S1), .S0(S0), .Y(Y[3]));
  MUX_1BIT mux_1bit_5 (.E0(E0[4]), .E1(E1[4]), .E2(E2[4]), .E3(E3[4]), .S1(S1), .S0(S0), .Y(Y[4]));
  MUX_1BIT mux_1bit_6 (.E0(E0[5]), .E1(E1[5]), .E2(E2[5]), .E3(E3[5]), .S1(S1), .S0(S0), .Y(Y[5]));
  MUX_1BIT mux_1bit_7 (.E0(E0[6]), .E1(E1[6]), .E2(E2[6]), .E3(E3[6]), .S1(S1), .S0(S0), .Y(Y[6]));
  MUX_1BIT mux_1bit_8 (.E0(E0[7]), .E1(E1[7]), .E2(E2[7]), .E3(E3[7]), .S1(S1), .S0(S0), .Y(Y[7]));
endmodule
