// Logisim project 1.1parte1_memoria.circ as structural Verilog: 1 circuit, main circuit main
module main (
  input  [5:0] in_1,
  input  [7:0] d_IN,
  input  we_ram,
  input  clk_ram,
  input  [7:0] d_in_reg,
  input  we_reg,
  input  clk_reg,
  output [7:0] saida_rom,
  output out_9,
  output out_10,
  output [7:0] dado_saida,
  output out_12,
  output out_13,
  output [7:0] saida_ram,
  output [7:0] saida_reg,
  output [7:0] out_16,
  output erro_paridade
);

  wire decodificador_enderecos_1_a4, decodificador_enderecos_1_a5, paridade_leitura_bit_paridade;
  wire [0:0] paridade8_1_bit_paridade;
  wire [3:0] decodificador_enderecos_1_a3_a0;

  paridade8 paridade8_1 (.dado(d_IN), .bit_paridade(paridade8_1_bit_paridade[0]));
  Decodificador_Enderecos decodificador_enderecos_1 (
    .ENDERECO(in_1), .A3_A0(decodificador_enderecos_1_a3_a0), .A5(decodificador_enderecos_1_a5),
    .out_4(out_9), .A4(decodificador_enderecos_1_a4), .out_6(out_10), .out_7(out_12), .out_8(out_13));
  ROM #(.addrWidth(4)) rom_1 (.addr(decodificador_enderecos_1_a3_a0), .data(saida_rom));
  memoriaRAM16by memoriaram16by_1 (
    .D(d_IN), .escrita(we_ram), .endereco(decodificador_enderecos_1_a3_a0), .clock(clk_ram), .saida(saida_ram));
  memoriaRAM16by BancoRegistradores (
    .D(d_in_reg), .escrita(we_reg), .endereco(decodificador_enderecos_1_a3_a0), .clock(clk_reg),
    .saida(saida_reg));
  memoriaRAM16by Arranjo_Paridade (
    .D({{7{1'b0}}, paridade8_1_bit_paridade[0]}), .escrita(we_ram),
    .endereco(decodificador_enderecos_1_a3_a0), .clock(clk_ram), .saida(out_16));
  paridade8 paridade_leitura (.dado(saida_ram), .bit_paridade(paridade_leitura_bit_paridade));
  XOR_1bit xor_1bit_1 (.A(paridade_leitura_bit_paridade), .B(out_16[0]), .S(erro_paridade));
  MUXX_8BITS muxx_8bits_1 (
    .S1(decodificador_enderecos_1_a5), .S0(decodificador_enderecos_1_a4), .E0(saida_rom), .E1(saida_ram),
    .E2(saida_reg), .E3({8{1'b0}}), .Y(dado_saida));

  // Notes on the sheet:
  //   contents of rom_1 (hex, n*v repeats v):
  //   11 22 33 44 55 66 77 88 99 aa bb cc dd ee ff
endmodule
