// Logisim project 1.2parte1_cache.circ as structural Verilog: 6 circuits, main circuit cachetop
module LinhaCache (
  input  [2:0] rotulo_in,
  input  escrever,
  input  clk,
  input  zerar,
  output [2:0] rotulo_out,
  output valido
);

  Register #(.width(3)) register_1 (.D(rotulo_in), .en(escrever), .clk(clk), .Q(rotulo_out), .clr(zerar));
  J_K_Flip_Flop j_k_ff_1 (.J(escrever), .K(1'b0), .clk(clk), .Q(valido), .reset(zerar));  // open: Qn, preset
endmodule

module cachelinhas (
  input  [1:0] indice,
  input  [2:0] rotulo_in,
  input  escrever,
  input  clk,
  input  zerar,
  output [2:0] rotulo_out,
  output valido
);

  wire and_1_out, and_2_out, and_3_out, and_4_out, decoder_1_out0, decoder_1_out1, decoder_1_out2,
       decoder_1_out3, linhacache_1_valido, linhacache_2_valido, linhacache_3_valido, linhacache_4_valido;
  wire [2:0] linhacache_1_rotulo_out, linhacache_2_rotulo_out, linhacache_3_rotulo_out,
       linhacache_4_rotulo_out;

  Decoder #(.enable("false"), .select(2)) decoder_1 (
    .out0(decoder_1_out0), .out1(decoder_1_out1), .out2(decoder_1_out2), .out3(decoder_1_out3), .sel(indice));
  and and_1 (and_1_out, decoder_1_out0, escrever);
  and and_2 (and_2_out, decoder_1_out1, escrever);
  and and_3 (and_3_out, decoder_1_out2, escrever);
  and and_4 (and_4_out, decoder_1_out3, escrever);
  Multiplexer #(.select(2), .width(3)) multiplexer_1 (
    .in0(linhacache_1_rotulo_out), .in1(linhacache_2_rotulo_out), .in2(linhacache_3_rotulo_out),
    .in3(linhacache_4_rotulo_out), .out(rotulo_out), .sel(indice));
  Multiplexer #(.select(2)) multiplexer_2 (
    .in0(linhacache_1_valido), .in1(linhacache_2_valido), .in2(linhacache_3_valido),
    .in3(linhacache_4_valido), .out(valido), .sel(indice));
  LinhaCache linhacache_1 (
    .rotulo_in(rotulo_in), .escrever(and_1_out), .clk(clk), .zerar(zerar),
    .rotulo_out(linhacache_1_rotulo_out), .valido(linhacache_1_valido));
  LinhaCache linhacache_2 (
    .rotulo_in(rotulo_in), .escrever(and_2_out), .clk(clk), .zerar(zerar),
    .rotulo_out(linhacache_2_rotulo_out), .valido(linhacache_2_valido));
  LinhaCache linhacache_3 (
    .rotulo_in(rotulo_in), .escrever(and_3_out), .clk(clk), .zerar(zerar),
    .rotulo_out(linhacache_3_rotulo_out), .valido(linhacache_3_valido));
  LinhaCache linhacache_4 (
    .rotulo_in(rotulo_in), .escrever(and_4_out), .clk(clk), .zerar(zerar),
    .rotulo_out(linhacache_4_rotulo_out), .valido(linhacache_4_valido));
endmodule

module cachecomparador (
  input  [2:0] tag_pedido,
  input  [2:0] tag_guardado,
  input  valido,
  output acerto
);

  wire not_1_out, or_1_out, xor_1bit_1_s, xor_1bit_2_s, xor_1bit_3_s;

  XOR_1bit xor_1bit_1 (.A(tag_pedido[0]), .B(tag_guardado[0]), .S(xor_1bit_1_s));
  XOR_1bit xor_1bit_2 (.A(tag_pedido[1]), .B(tag_guardado[1]), .S(xor_1bit_2_s));
  XOR_1bit xor_1bit_3 (.A(tag_pedido[2]), .B(tag_guardado[2]), .S(xor_1bit_3_s));
  or or_1 (or_1_out, xor_1bit_1_s, xor_1bit_2_s, xor_1bit_3_s);
  not not_1 (not_1_out, or_1_out);
  and and_1 (acerto, not_1_out, valido);
endmodule

module cachetop (
  input  [5:0] endereco,
  input  leitura,
  input  clk,
  input  zerar,
  output [2:0] rotulo_linha,
  output [3:0] contadorAcerto,
  output acerto
);

  wire and_1_out, and_2_out, cachelinhas_1_valido, not_1_out, not_2_out;

  not not_1 (not_1_out, acerto);
  and and_1 (and_1_out, leitura, not_1_out);
  not not_2 (not_2_out, clk);
  cachelinhas cachelinhas_1 (
    .indice(endereco[2:1]), .rotulo_in(endereco[5:3]), .escrever(and_1_out), .clk(not_2_out), .zerar(zerar),
    .rotulo_out(rotulo_linha), .valido(cachelinhas_1_valido));
  cachecomparador cachecomparador_1 (
    .tag_pedido(endereco[5:3]), .tag_guardado(rotulo_linha), .valido(cachelinhas_1_valido), .acerto(acerto));
  Counter #(.max('hf), .width(4)) counter_1 (
    .clr(zerar), .count(and_2_out), .clk(clk), .Q(contadorAcerto));  // open: load, up, D, carry
  and and_2 (and_2_out, acerto, leitura);
  Hex_Digit_Display hex_digit_display_1 (.value(contadorAcerto));  // open: dp
endmodule

module calc_endereco (
  input  [7:0] base,
  input  [7:0] deslocamento,
  output [7:0] soma,
  output cout,
  output [5:0] endereco_cache
);

  Adder adder_1 (.a(base), .b(deslocamento), .out({soma[7:6], endereco_cache}), .cout(cout));  // open: cin

  assign soma[5:0] = endereco_cache;
endmodule

module teste_conflito (
  input  zerar,
  input  clk_v,
  input  clk_cache,
  output [2:0] v,
  output [5:0] endereco_gerado,
  output [2:0] out_6,
  output [3:0] out_7,
  output primo,
  output out_9
);

  wire [5:0] calc_endereco_1_endereco_cache;
  wire [7:0] bit_extender_1_out;

  Counter #(.max('h7), .width(3)) counter_1 (
    .clr(zerar), .clk(clk_v), .Q(endereco_gerado[5:3]));  // open: load, up, count, D, carry
  assign bit_extender_1_out = {{2{1'b0}}, {endereco_gerado[5:3], 3'b000}};  // Bit_Extender bit_extender_1
  detector detector_1 (.Entrada({1'b0, endereco_gerado[5:3]}), .primo(primo));
  calc_endereco calc_endereco_1 (
    .base(bit_extender_1_out), .deslocamento({8{1'b0}}), .endereco_cache(calc_endereco_1_endereco_cache));  // open: soma, cout
  cachetop cachetop_1 (
    .endereco(calc_endereco_1_endereco_cache), .leitura(primo), .clk(clk_cache), .zerar(zerar),
    .rotulo_linha(out_6), .contadorAcerto(out_7), .acerto(out_9));

  assign endereco_gerado[2:0] = 3'b000;
  assign v = endereco_gerado[5:3];
endmodule
