// Logisim project parte2_microprogramada.circ as structural Verilog: 2 circuits, main circuit Unidade_Controle_Cabeada
// D2
module Unidade_Controle_Cabeada (
  input  CLOCK,
  input  RESET,
  input  [5:0] OPCODE,
  input  ZERO,
  output S1,
  output S0,
  output [1:0] Acao,
  output PCWr,
  output [1:0] Fonte,
  output ALUOp_0,
  output SrcB_0,
  output ALUOp_1,
  output [1:0] ULAOp,
  output SrcA,
  output PCSrc,
  output SrcB_1,
  output PCWrC,
  output IRWr,
  output MemRd,
  output RegWr
);

  wire not_1_out, not_2_out, not_3_out, not_4_out, not_5_out, or_1_out;
  wire [2:0] counter_1_q;
  wire [2:1] SALTO_TIPO_R_out;
  wire [3:0] bit_extender_1_out;

  not not_1 (not_1_out, OPCODE[2]);
  and and_1 (SrcB_1, Fonte[0], not_2_out);
  not not_2 (not_2_out, Fonte[0]);
  not not_3 (not_3_out, Fonte[1]);
  and and_2 (SrcA, Fonte[0], not_3_out);
  and SALTO_BEQ (SALTO_TIPO_R_out[2], S1, OPCODE[2]);
  and SALTO_TIPO_R (SALTO_TIPO_R_out[1], not_1_out, S1);
  and and_3 (PCWr, not_2_out, not_3_out);
  not not_4 (not_4_out, Acao[0]);
  not not_5 (not_5_out, Acao[1]);
  and and_4 (RegWr, not_4_out, Acao[1]);
  Counter #(.max('h7), .width(3)) counter_1 (
    .clr(RESET), .load(or_1_out), .clk(CLOCK), .D({SALTO_TIPO_R_out, 1'b0}), .Q(counter_1_q));  // open: up, count, carry
  ROM #(.addrWidth(3)) rom_1 (.addr(counter_1_q), .data({ALUOp_1, ALUOp_0, Fonte, Acao, S1, S0}));
  or or_1 (or_1_out, S1, S0);
  and and_5 (IRWr, Acao[0], not_5_out);
  and and_6 (PCSrc, Acao[0], Acao[1]);
  assign bit_extender_1_out = {{1{1'b0}}, counter_1_q};  // Bit_Extender bit_extender_1
  and and_7 (PCWrC, ZERO, PCSrc);
  Hex_Digit_Display hex_digit_display_1 (.value(bit_extender_1_out));  // open: dp

  assign MemRd = IRWr;
  assign SrcB_0 = PCWr;
  assign ULAOp = {ALUOp_1, ALUOp_0};

  // Notes on the sheet:
  //   contents of rom_1 (hex, n*v repeats v):
  //   4 22 90 39 5d
endmodule

module Registrador_FLIP_FLOP_D_661eac99 (
  input  CLK,
  input  D,
  output Q,
  output Q_NEGADO
);

  wire and_1_out, and_2_out, not_1_out;

  not not_1 (not_1_out, D);
  and and_1 (and_1_out, not_1_out, CLK);
  and and_2 (and_2_out, CLK, D);
  nor nor_1 (Q, and_1_out, Q_NEGADO);
  nor nor_2 (Q_NEGADO, Q, and_2_out);
endmodule
